# Fritzing sketch diagrama_esquematico_ligacao (saved by Fritzing 0.9.2b)

parts:
  DI1 = 7-Segment LED Display [package=THT]
  R1 = Resistor [tolerance=±5% resistance=100 package=THT]
  Componente1 = Arduino Uno (Rev3) - ICSP

nets:
  N1: DI1.cathodeE, Componente1.D6_PWM
  N2: DI1.cathodeD, Componente1.D5_PWM
  N3: DI1.commAnode, R1.Pin_0
  N4: DI1.cathodeC, Componente1.D4
  N5: DI1.cathodeDP, Componente1.D9_PWM
  N6: DI1.cathodeB, Componente1.D3_PWM
  N7: DI1.cathodeA, Componente1.D2
  N8: DI1.cathodeF, Componente1.D7
  N9: DI1.cathodeG, Componente1.D8
  N10: R1.Pin_1, Componente1.5V

notes:
  5V
  6
  10
  1
  5
  100 ohms
  Anodo comum
